# Fritzing sketch sonar-circuit (saved by Fritzing 0.9.2b)
breadboards: 1

parts:
  Part3 = SRF05 Ultrasonic Rangefinder
  Raspberry_Pi1 = Raspberry Pi B+
  R1 = Resistor [tolerance=±5% resistance=2.2k package=THT]
  R2 = Resistor [tolerance=±5% resistance=1k package=THT]
  R3 = Resistor [tolerance=±5% resistance=2.2k package="1206 [SMD]"]

nets:
  VCC: Part3.VCC, Raspberry_Pi1.5V
  N1: Part3.Trig, R2.Pin_0
  N2: Part3.Echo, R3.Pin_0
  N3: Raspberry_Pi1.GND, R1.Pin_1
  N4: Raspberry_Pi1.GPIO20, R1.Pin_0, R2.Pin_1, R3.Pin_1
